# Fritzing sketch SlowMotionShowdown (saved by Fritzing 1.0.1rc)
breadboards: 2

parts:
  A1 = Particle - Photon2
  S7 = Pushbutton [package="[THT]"]
  S8 = Pushbutton [package="[THT]"]
  S9 = Pushbutton [package="[THT]"]
  S10 = Pushbutton [package="[THT]"]
  S5 = Pushbutton [package="[THT]"]
  Part1 = HC-SR501 Body Sensor Module
  Part2 = HC-SR501 Body Sensor Module
  Neopixel1 = Adafruit RBG Smart Neopixel [package="DIP (Dual Inline) [THT]"]
  S6 = Pushbutton [package="[THT]"]
  Neopixel2 = Adafruit RBG Smart Neopixel [package="DIP (Dual Inline) [THT]"]
  OLED_I2C1 = OLED 128x64 I2C Monochrome Display
  S11 = Taiway 100-SP-X-T1 SPDT Miniature Toggle Switch [part_number=100-SP-X-T1-0-0-B1-M2 package=THT]

nets:
  3.3V: A1.Pin_2, Part1.VCC, Part2.VCC, OLED_I2C1.VDD, S11.L2
  GND: A1.Pin_4, A1.Pin_30, S10.Pin_3, S10.Pin_4, S5.Pin_3, S5.Pin_4, Part1.GND, Part2.GND, Neopixel1.G, S6.Pin_3, S6.Pin_4, Neopixel2.G, OLED_I2C1.GND, S11.L1
  N1: A1.Pin_5, S5.Pin_1, S5.Pin_2
  N2: A1.Pin_6, S6.Pin_1, S6.Pin_2
  N3: A1.Pin_7, S7.Pin_1, S7.Pin_2
  N4: A1.Pin_8, S11.COM
  N5: A1.Pin_17, OLED_I2C1.SDA
  N6: A1.Pin_18, OLED_I2C1.SCK
  N7: A1.Pin_19, Neopixel1.In
  N8: A1.Pin_24, Part2.OUT
  N9: A1.Pin_25, Part1.OUT
  5V: A1.Pin_26, Neopixel1.+, Neopixel2.+
  N10: S7.Pin_3, S7.Pin_4, S8.Pin_1, S8.Pin_2
  N11: S8.Pin_3, S8.Pin_4, S9.Pin_1, S9.Pin_2
  N12: S9.Pin_3, S9.Pin_4, S10.Pin_1, S10.Pin_2
  N13: Neopixel1.O, Neopixel2.In

notes:
  2 buttons for each player to place their hand before each round starts.
  Switch to toggle between manual/automatic
  One motion sensor pointed at each player.
  2 3D printed resin shapes illuminated by neopixels
  The button each player is trying to press.

custom parts:
  Particle - Photon2: The Photon 2 is a microcontroller and Wi-Fi networking developed by particle. Features: 802.11a/b/g/n Wi-Fi, 2.4 GHz and 5 GHz Integrated PCB antenna Integrated U.FL connector for external antenna Integrated RF switch BLE 5 using same antenna as Wi-Fi Realtek RTL8721DM MCU ARM Cortex M33 CPU, 200 MHz 2048 KB (2 MB) user application maximum size 3072 KB (3 MB) of RAM available to user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
  Pushbutton: A generic pushbutton.
  Pushbutton: A generic pushbutton.
  HC-SR501 Body Sensor Module: Pyroelectric Infrared PIR Motion Sensor Detector Module
  Pushbutton: A generic pushbutton.
